# Fritzing sketch pushButton (saved by Fritzing 0.9.3b)
breadboards: 2

parts:
  INPUT_PULLUP = Arduino Uno (Rev3)
  S1 = Pushbutton [package="[THT]"]
  INPUT_PULLUP1 = Arduino Uno (Rev3)
  S2 = Pushbutton [package="[THT]"]
  R1 = Resistor [tolerance=±5% resistance=10k package=THT]

nets:
  N1: INPUT_PULLUP.D2, S1.Pin_1, S1.Pin_2
  N2: INPUT_PULLUP.GND, S1.Pin_3, S1.Pin_4
  N3: INPUT_PULLUP1.D2, S2.Pin_3, S2.Pin_4, R1.Pin_1
  N4: INPUT_PULLUP1.5V, S2.Pin_1, S2.Pin_2

notes:
  pinMode ( INPUT_PULLUP )
  pinMode ( INPUT )
  R 10kΩ
